# Fritzing sketch Layout (saved by Fritzing 1.0.1rc)

parts:
  Part1 = Arduino Uno (Rev3)-TopMount
  Part2 = Arduino Nano (Rev3.0)
  Part3 = Adafruit TCA9548A
  A1 = AS5600 module
  A2 = AS5600 module
  A3 = AS5600 module
  A4 = AS5600 module
  A5 = AS5600 module
  A6 = AS5600 module

nets:
  N1: Part1.D10_PWM/SS, Part2.D10
  N2: Part1.D11_PWM/MOSI, Part2.D11/MOSI
  N3: Part1.D12/MISO, Part2.D12/MISO
  N4: Part1.D13/SCK, Part2.D13/SCK
  GND: Part1.GND, Part2.GND, Part3.GND, A1.Pin_3, A2.Pin_3, A3.Pin_3, A4.Pin_3, A5.Pin_3, A6.Pin_3
  5V: Part1.5V, Part2.5V, Part3.VCC, A1.Pin_1, A2.Pin_1, A3.Pin_1, A4.Pin_1, A5.Pin_1, A6.Pin_1
  N5: Part2.A5, Part3.INPUTSCL
  N6: Part2.A4, Part3.INPUTSDA
  N7: Part3.2SDA, A3.Pin_5
  N8: Part3.2SCL, A3.Pin_6
  N9: Part3.3SDA, A5.Pin_5
  N10: Part3.3SCL, A5.Pin_6
  N11: Part3.4SDA, A2.Pin_5
  N12: Part3.4SCL, A2.Pin_6
  N13: Part3.5SDA, A4.Pin_5
  N14: Part3.5SCL, A4.Pin_6
  N15: Part3.0SDA, A6.Pin_5
  N16: Part3.0SCL, A6.Pin_6
  N17: Part3.1SDA, A1.Pin_5
  N18: Part3.1SCL, A1.Pin_6

custom parts:
  Arduino Uno (Rev3)-TopMount: Arduino Uno (Rev3) for Top PCB Mount. The PCB view of the Arduino Uno (Rev3) in Arduino Bin flipped upside down with the text flipped back so as to be readable. Other views haven't changed Protruding component position is outlined to provide indication of part contact. Number in component outline is mm of protrusion of the component from the UNO PCB. Subtract the number from the USB (11mm),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
  Adafruit TCA9548A: You just found the perfect I2C sensor, and you want to wire up two or three or more of them to your Arduino when you realize "Uh oh, this chip has a fixed I2C address, and from what I know about I2C, you cannot have two devices with the same address on the same SDA/SCL pins!" Are you out of luck? You would be, if you didn't have this ultra-cool TCA9548A 1-to-8 I2C multiplexer! Finally, a way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
  AS5600 module: .This module is mainly placed behind the stepper motor to obtain the rotation angle of the stepper motor.
